# Fritzing sketch google assistance (saved by Fritzing 0.8.7b)
breadboards: 1

parts:
  KY-1 = Keyes Relay [package=THT]
  KY-2 = Keyes Relay [package=THT]
  U1 = NodeMCU V3.0
  LED1 = LED - 5mm [color="Red (633nm)" package="5 mm [THT]"]
  R2 = Resistor [tolerance=±5% resistance=220 package=THT]
  VCC2 = Battery
  LED3 = LEDs [package=led10mm]

nets:
  N1: KY-1.signal, U1.D5
  N2: KY-1.power, KY-1.C, U1.Vin, VCC2.+
  N3: KY-1.ground, LED1.anode, VCC2.-
  N4: KY-1.NO, R2.Pin_0
  N5: KY-2.signal, U1.D6
  N6: KY-2.NO, LED3.A
  N7: U1.GND#6, U1.GND#13, U1.GND#16, U1.GND#33

custom parts:
  Keyes Relay: The Keyes 5V relay module is suitable for SCM development, home appliance control. It uses a 5V~12V TIL control signal which can control DC / AC signal.
  NodeMCU V3.0: ESP8266 based NodeMCU
  LEDs: LEDs Standard schematic elements and footprints for 5mm, 3mm, 1206, and 0603 sized LEDs. 5mm - Spark Fun Electronics SKU : COM-00529 (and others)
